// Digital circuit FINALALUDESIGN.dig as structural Verilog
module FINALALUDESIGN (
  input  [3:0] S,
  input  in_2,
  input  in_3,
  input  in_4,
  input  in_5,
  input  in_6,
  input  in_8,
  input  X0,
  input  X1,
  input  X2,
  input  X3,
  input  Y0,
  input  Y1,
  input  Y2,
  input  Y3,
  input  in_24,
  input  _1,
  input  _0,
  input  _3,
  input  [6:0] _0_2,
  input  [6:0] _0_3,
  input  [6:0] _4,
  input  [3:0] in_32,
  input  [3:0] in_33,
  input  [3:0] in_34,
  input  [3:0] in_35,
  input  [7:0] in_36,
  input  [3:0] in_37,
  input  [3:0] in_38,
  input  [3:0] in_39,
  input  [3:0] in_40,
  output [7:0] Output,
  output Q3,
  output Q2,
  output Q1,
  output Q0,
  output R5,
  output R4,
  output R3,
  output out_26
);

  wire and_2_out, and_3_out, and_4_out, and_5_out, and_6_out, and_7_out, and_8_out, and_13_out, and_14_out,
       and_15_out, and_16_out, and_17_out, and_18_out, and_19_out, and_20_out, and_21_out, and_22_out,
       and_23_out, and_24_out, and_25_out, and_26_out, and_27_out, and_28_out, and_29_out, and_30_out,
       and_31_out, and_32_out, and_33_out, and_34_out, and_35_out, and_36_out, and_37_out, and_39_out,
       and_40_out, and_41_out, and_42_out, and_43_out, and_44_out, and_45_out, and_46_out, and_47_out,
       and_48_out, and_49_out, and_50_out, and_52_out, and_53_out, and_55_out, and_56_out, and_58_out,
       and_59_out, and_61_out, and_62_out, and_63_out, and_64_out, and_65_out, and_66_out, and_67_out,
       and_68_out, and_69_out, and_70_out, and_71_out, and_73_out, and_74_out, and_75_out, and_76_out,
       and_77_out, and_78_out, and_79_out, and_80_out, and_81_out, and_82_out, and_83_out, and_84_out,
       and_85_out, and_86_out, and_87_out, and_88_out, and_89_out, and_90_out, and_91_out, and_92_out,
       and_93_out, and_94_out, and_95_out, and_96_out, and_97_out, and_98_out, and_99_out, and_100_out,
       and_101_out, and_102_out, and_103_out, and_104_out, and_105_out, and_106_out, and_107_out,
       and_108_out, and_109_out, and_110_out, and_111_out, and_112_out, and_113_out, and_114_out,
       and_115_out, and_116_out, and_117_out, and_118_out, and_119_out, and_120_out, and_121_out,
       and_122_out, and_123_out, and_124_out, and_125_out, and_126_out, and_127_out, and_128_out,
       and_129_out, and_130_out, and_131_out, and_132_out, and_133_out, and_134_out, and_135_out,
       and_136_out, and_137_out, and_138_out, and_139_out, and_140_out, and_141_out, and_142_out,
       and_143_out, and_144_out, and_145_out, and_146_out, and_147_out, and_148_out, and_150_out,
       and_151_out, and_152_out, and_153_out, and_154_out, and_155_out, and_156_out, and_157_out,
       and_158_out, and_159_out, and_160_out, and_161_out, and_162_out, and_163_out, and_164_out,
       and_165_out, and_166_out, and_167_out, and_168_out, and_169_out, nor_1_out, nor_2_out, nor_3_out,
       nor_4_out, not_1_out, not_2_out, not_3_out, not_4_out, not_5_out, not_6_out, not_7_out, not_8_out,
       not_9_out, not_10_out, not_11_out, not_12_out, not_13_out, not_14_out, not_15_out, not_16_out,
       not_17_out, not_18_out, not_19_out, not_24_out, not_25_out, not_26_out, not_27_out, not_28_out,
       not_29_out, not_30_out, not_31_out, not_32_out, or_18_out, or_19_out, or_22_out, or_23_out, or_24_out,
       or_26_out, or_28_out, or_29_out, or_31_out, or_32_out, or_33_out, or_35_out, or_36_out, or_37_out,
       or_38_out, or_39_out, or_40_out, or_41_out, xor_10_out, xor_13_out, xor_15_out, xor_16_out,
       xor_20_out, xor_21_out, xor_22_out, xor_26_out, xor_27_out, xor_28_out, xor_30_out, xor_31_out,
       xor_32_out, xor_33_out, xor_34_out, xor_35_out, xor_37_out, xor_38_out, xor_39_out, xor_40_out;
  wire [0:0] and_72_out, or_16_out, or_17_out;
  wire [3:0] and_9_out, and_51_out, and_57_out, not_20_out, or_3_out, or_4_out, xor_3_out;
  wire [4:0] xor_1_out, xor_11_out;
  wire [7:0] xor_9_out, xor_18_out;

  not not_1 (not_1_out, Y0);
  not not_2 (not_2_out, Y1);
  not not_3 (not_3_out, Y2);
  not not_4 (not_4_out, X0);
  not not_5 (not_5_out, X1);
  not not_6 (not_6_out, X2);
  not not_7 (not_7_out, X3);
  and and_1 (Q3, X3, Y0, not_2_out, not_3_out);
  and and_2 (and_2_out, X2, Y0, not_2_out, not_3_out);
  or or_1 (Q2, and_2_out, and_3_out, and_4_out);
  and and_3 (and_3_out, X2, X3, Y0, not_3_out);
  and and_4 (and_4_out, X3, not_1_out, Y1, not_3_out);
  and and_5 (and_5_out, X1, X2, not_7_out, Y0, not_3_out);
  and and_6 (and_6_out, X1, Y0, not_2_out, not_3_out);
  and and_7 (and_7_out, X1, X3, Y0, not_2_out);
  and and_8 (and_8_out, X1, X2, X3, Y2);
  xor xor_1 (xor_1_out[0], _1, X0);
  or or_2 (Q1, and_5_out, and_6_out, and_7_out, and_8_out, and_14_out, and_15_out, and_18_out, and_21_out, and_24_out);
  and and_9 (and_9_out[0], X0, Y0);
  and and_10 (and_9_out[1], X1, Y1);
  and and_11 (and_9_out[2], X2, Y2);
  and and_12 (and_9_out[3], X3, Y3);
  and and_13 (and_13_out, _1, X0);
  and and_14 (and_14_out, not_6_out, X3, Y0, Y1, not_3_out);
  not not_8 (not_8_out, X0);
  not not_9 (not_9_out, X1);
  not not_10 (not_10_out, X2);
  not not_11 (not_11_out, X3);
  and and_15 (and_15_out, X2, not_1_out, Y1, not_3_out);
  and and_16 (and_16_out, X0, X3);
  and and_17 (and_17_out, X1, X3);
  and and_18 (and_18_out, X2, X3, not_1_out, Y1);
  or or_3 (or_3_out[3], and_16_out, and_17_out, and_19_out);
  and and_19 (and_19_out, X2, X3);
  xor xor_2 (xor_1_out[1], and_13_out, X1);
  and and_20 (and_20_out, and_13_out, X1);
  and and_21 (and_21_out, X2, X3, not_2_out, Y2);
  or or_4 (or_4_out[0], X0, Y0);
  or or_5 (or_4_out[1], X1, Y1);
  or or_6 (or_4_out[2], X2, Y2);
  or or_7 (or_4_out[3], X3, Y3);
  and and_22 (and_22_out, X0, X2);
  and and_23 (and_23_out, not_8_out, not_9_out, not_10_out, X3);
  and and_24 (and_24_out, X3, not_1_out, not_2_out, Y2);
  or or_8 (or_3_out[2], and_22_out, and_23_out, and_26_out);
  and and_25 (and_25_out, X0, X1, X2, Y0, not_2_out);
  and and_26 (and_26_out, X1, X2);
  xor xor_3 (xor_3_out[0], X0, Y0);
  xor xor_4 (xor_3_out[1], X1, Y1);
  xor xor_5 (xor_3_out[2], X2, Y2);
  xor xor_6 (xor_3_out[3], X3, Y3);
  and and_27 (and_27_out, X0, X1);
  xor xor_7 (xor_1_out[2], and_20_out, X2);
  and and_28 (and_28_out, and_20_out, X2);
  and and_29 (and_29_out, X0, X2, not_7_out, Y0, not_2_out);
  or or_9 (or_3_out[1], and_27_out, and_30_out, and_32_out);
  and and_30 (and_30_out, not_8_out, not_9_out, X2);
  and and_31 (and_31_out, X0, not_6_out, X3, Y0, Y1);
  and and_32 (and_32_out, not_8_out, not_9_out, X3);
  and and_33 (and_33_out, not_8_out, X1);
  and and_34 (and_34_out, X0, X1, not_6_out, Y0, not_3_out);
  and and_35 (and_35_out, not_8_out, X2);
  and and_36 (and_36_out, X0, X1, X3, Y0, not_3_out);
  not not_12 (not_12_out, X3);
  not not_13 (not_13_out, Y3);
  not not_14 (not_14_out, X2);
  not not_15 (not_15_out, Y2);
  not not_16 (not_16_out, X1);
  not not_17 (not_17_out, Y1);
  not not_18 (not_18_out, X0);
  not not_19 (not_19_out, Y0);
  not not_20 (not_20_out[0], X0);
  not not_21 (not_20_out[1], X1);
  not not_22 (not_20_out[2], X2);
  not not_23 (not_20_out[3], X3);
  or or_10 (or_3_out[0], and_33_out, and_35_out, and_37_out, and_39_out);
  and and_37 (and_37_out, not_8_out, X3);
  xor xor_8 (xor_1_out[3], and_28_out, X3);
  and and_38 (xor_1_out[4], and_28_out, X3);
  and and_39 (and_39_out, X1, X2, not_11_out);
  and and_40 (and_40_out, X0, X1, X2, not_7_out, Y2);
  not not_24 (not_24_out, _3);
  not not_25 (not_25_out, _0);
  and and_41 (and_41_out, not_12_out, Y3);
  and and_42 (and_42_out, X3, not_13_out);
  and and_43 (and_43_out, not_14_out, Y2);
  and and_44 (and_44_out, X2, not_15_out);
  and and_45 (and_45_out, not_16_out, Y1);
  and and_46 (and_46_out, X1, not_17_out);
  and and_47 (and_47_out, not_18_out, Y0);
  and and_48 (and_48_out, X0, not_19_out);
  and and_49 (and_49_out, X0, Y0, not_2_out, not_3_out);
  and and_50 (and_50_out, X3, not_24_out);
  and and_51 (and_51_out[3], _3, X2);
  and and_52 (and_52_out, X2, not_24_out);
  and and_53 (and_53_out, _3, X1);
  and and_54 (and_51_out[0], X1, not_24_out);
  and and_55 (and_55_out, _3, X0);
  and and_56 (and_56_out, X3, not_25_out);
  and and_57 (and_57_out[3], _0, X2);
  and and_58 (and_58_out, X2, not_25_out);
  and and_59 (and_59_out, _0, X1);
  and and_60 (and_57_out[0], X1, not_25_out);
  and and_61 (and_61_out, _0, X0);
  or or_11 (Q0, and_25_out, and_29_out, and_31_out, and_34_out, and_36_out, and_40_out, and_49_out, and_62_out, and_65_out, and_74_out, and_75_out, and_76_out, and_78_out, and_80_out, and_82_out, and_84_out);
  nor nor_1 (nor_1_out, and_41_out, and_42_out);
  nor nor_2 (nor_2_out, and_43_out, and_44_out);
  nor nor_3 (nor_3_out, and_45_out, and_46_out);
  nor nor_4 (nor_4_out, and_47_out, and_48_out);
  not not_26 (not_26_out, X0);
  not not_27 (not_27_out, X1);
  and and_62 (and_62_out, not_5_out, X2, not_7_out, Y0, Y1, not_3_out);
  xor xor_9 (xor_9_out[0], X0, Y0);
  and and_63 (and_63_out, not_26_out, Y0);
  xor xor_10 (xor_10_out, X1, Y1);
  and and_64 (and_64_out, not_27_out, Y1);
  and and_65 (and_65_out, not_5_out, X3, Y0, Y1, Y2);
  or or_12 (and_51_out[2], and_50_out, and_53_out);
  or or_13 (and_51_out[1], and_52_out, and_55_out);
  or or_14 (and_57_out[2], and_56_out, and_59_out);
  or or_15 (and_57_out[1], and_58_out, and_61_out);
  and and_66 (and_66_out, nor_1_out, and_43_out);
  and and_67 (and_67_out, nor_1_out, and_44_out);
  and and_68 (and_68_out, nor_1_out, nor_2_out, and_45_out);
  and and_69 (and_69_out, nor_1_out, nor_2_out, and_46_out);
  and and_70 (and_70_out, nor_1_out, nor_2_out, nor_3_out, and_47_out);
  and and_71 (and_71_out, nor_1_out, nor_2_out, nor_3_out, and_48_out);
  and and_72 (and_72_out[0], nor_1_out, nor_2_out, nor_3_out, nor_4_out);
  and and_73 (and_73_out, X0, Y0);
  xor xor_11 (xor_11_out[0], Y0, X0);
  not not_28 (not_28_out, xor_10_out);
  and and_74 (and_74_out, X1, X2, not_7_out, not_1_out, Y1);
  xor xor_12 (xor_9_out[1], and_63_out, xor_10_out);
  and and_75 (and_75_out, not_5_out, not_6_out, X3, Y0, Y2);
  or or_16 (or_16_out[0], and_41_out, and_66_out, and_68_out, and_70_out);
  or or_17 (or_17_out[0], and_42_out, and_67_out, and_69_out, and_71_out);
  and and_76 (and_76_out, X1, X2, not_7_out, not_2_out, Y2);
  and and_77 (and_77_out, and_73_out, X1);
  xor xor_13 (xor_13_out, X1, and_73_out);
  and and_78 (and_78_out, X1, not_1_out, Y1, not_3_out);
  and and_79 (and_79_out, and_63_out, not_28_out);
  and and_80 (and_80_out, X1, not_6_out, X3, Y1);
  and and_81 (and_81_out, xor_13_out, Y1);
  xor xor_14 (xor_11_out[1], Y1, xor_13_out);
  or or_18 (or_18_out, and_79_out, and_64_out);
  not not_29 (not_29_out, X2);
  and and_82 (and_82_out, X2, not_1_out, not_2_out, Y2);
  xor xor_15 (xor_15_out, X2, Y2);
  and and_83 (and_83_out, not_29_out, Y2);
  and and_84 (and_84_out, not_6_out, X3, Y1, Y2);
  or or_19 (or_19_out, and_77_out, and_81_out);
  not not_30 (not_30_out, xor_15_out);
  and and_85 (and_85_out, X0, not_5_out, not_6_out, X3, Y0, not_2_out, Y2);
  and and_86 (and_86_out, or_19_out, X2);
  xor xor_16 (xor_16_out, X2, or_19_out);
  xor xor_17 (xor_9_out[2], or_18_out, xor_15_out);
  and and_87 (and_87_out, not_4_out, X1, X2, X3, Y0, not_2_out, Y2);
  and and_88 (and_88_out, not_4_out, X2, not_7_out, Y0, Y1, Y2);
  xor xor_18 (xor_18_out[6], or_26_out, xor_20_out);
  and and_89 (and_89_out, xor_16_out, Y2);
  xor xor_19 (xor_11_out[2], Y2, xor_16_out);
  and and_90 (and_90_out, xor_20_out, or_26_out);
  and and_91 (and_91_out, or_18_out, not_30_out);
  and and_92 (and_92_out, not_4_out, not_5_out, X2, not_7_out, Y0, Y2);
  xor xor_20 (xor_20_out, and_105_out, or_24_out);
  not not_31 (not_31_out, X3);
  or or_20 (R5, and_85_out, and_87_out, and_88_out, and_92_out, and_95_out, and_96_out, and_98_out, and_99_out, and_101_out);
  and and_93 (and_93_out, or_24_out, and_105_out);
  or or_21 (xor_18_out[7], and_93_out, and_90_out);
  or or_22 (or_22_out, and_86_out, and_89_out);
  or or_23 (or_23_out, and_91_out, and_83_out);
  and and_94 (and_94_out, not_31_out, Y3);
  and and_95 (and_95_out, X0, X1, not_6_out, Y1, Y2);
  xor xor_21 (xor_21_out, X3, Y3);
  and and_96 (and_96_out, X0, X1, not_6_out, not_7_out, Y2);
  and and_97 (and_97_out, or_22_out, X3);
  xor xor_22 (xor_22_out, X3, or_22_out);
  not not_32 (not_32_out, xor_21_out);
  and and_98 (and_98_out, X1, not_6_out, X3, not_1_out, Y1, Y2);
  xor xor_23 (xor_9_out[3], or_23_out, xor_21_out);
  xor xor_24 (xor_18_out[5], xor_26_out, xor_27_out);
  and and_99 (and_99_out, not_5_out, X2, Y0, Y1, Y2);
  and and_100 (and_100_out, xor_22_out, Y3);
  xor xor_25 (xor_11_out[3], Y3, xor_22_out);
  and and_101 (and_101_out, not_5_out, X2, not_7_out, Y1, Y2);
  and and_102 (and_102_out, xor_27_out, xor_26_out);
  xor xor_26 (xor_26_out, and_118_out, xor_28_out);
  xor xor_27 (xor_27_out, and_109_out, or_28_out);
  and and_103 (and_103_out, X0, not_5_out, X2, not_7_out, Y0, Y1, not_3_out);
  and and_104 (and_104_out, xor_28_out, and_118_out);
  and and_105 (and_105_out, Y3, X3);
  and and_106 (and_106_out, or_28_out, and_109_out);
  or or_24 (or_24_out, and_106_out, and_102_out);
  or or_25 (xor_11_out[4], and_97_out, and_100_out);
  and and_107 (and_107_out, or_23_out, not_32_out);
  xor xor_28 (xor_28_out, and_113_out, or_29_out);
  and and_108 (and_108_out, not_4_out, not_5_out, not_6_out, X3, Y0, Y1, not_3_out);
  or or_26 (or_26_out, and_110_out, and_104_out);
  and and_109 (and_109_out, Y3, X2);
  or or_27 (xor_9_out[7], and_107_out, and_94_out);
  and and_110 (and_110_out, or_29_out, and_113_out);
  xor xor_29 (xor_18_out[4], xor_30_out, xor_31_out);
  and and_111 (and_111_out, X0, X1, not_6_out, X3, Y0, Y1, not_3_out);
  and and_112 (and_112_out, xor_31_out, xor_30_out);
  and and_113 (and_113_out, Y2, X3);
  xor xor_30 (xor_30_out, xor_33_out, xor_32_out);
  xor xor_31 (xor_31_out, and_116_out, and_124_out);
  and and_114 (and_114_out, not_4_out, X1, X2, X3, Y0, Y1, not_3_out);
  and and_115 (and_115_out, xor_32_out, xor_33_out);
  and and_116 (and_116_out, Y3, X1);
  and and_117 (and_117_out, and_124_out, and_116_out);
  or or_28 (or_28_out, and_117_out, and_112_out);
  and and_118 (and_118_out, or_31_out, and_121_out);
  and and_119 (and_119_out, Y2, X2);
  xor xor_32 (xor_32_out, and_119_out, or_32_out);
  and and_120 (and_120_out, not_4_out, X1, not_6_out, Y0, Y1, Y2);
  and and_121 (and_121_out, Y1, X3);
  and and_122 (and_122_out, or_32_out, and_119_out);
  or or_29 (or_29_out, and_122_out, and_115_out);
  xor xor_33 (xor_33_out, or_31_out, and_121_out);
  and and_123 (and_123_out, not_4_out, X1, not_7_out, Y0, Y1, Y2);
  xor xor_34 (xor_34_out, and_125_out, xor_37_out);
  xor xor_35 (xor_35_out, xor_34_out, xor_38_out);
  and and_124 (and_124_out, and_129_out, xor_35_out);
  and and_125 (and_125_out, Y1, X2);
  and and_126 (and_126_out, xor_37_out, and_125_out);
  and and_127 (and_127_out, Y2, X1);
  and and_128 (and_128_out, xor_38_out, xor_34_out);
  and and_129 (and_129_out, Y3, X0);
  xor xor_36 (xor_18_out[3], and_129_out, xor_35_out);
  and and_130 (and_130_out, not_4_out, not_5_out, X3, Y0, not_2_out, Y2);
  and and_131 (and_131_out, Y0, X3);
  xor xor_37 (xor_37_out, and_131_out, or_33_out);
  xor xor_38 (xor_38_out, and_127_out, and_137_out);
  or or_30 (R4, and_103_out, and_108_out, and_111_out, and_114_out, and_120_out, and_123_out, and_130_out, and_134_out, and_138_out, and_142_out, and_144_out, and_147_out, and_148_out, and_150_out, and_151_out, and_152_out);
  and and_132 (and_132_out, or_33_out, and_131_out);
  or or_31 (or_31_out, and_132_out, and_126_out);
  and and_133 (and_133_out, and_137_out, and_127_out);
  or or_32 (or_32_out, and_133_out, and_128_out);
  and and_134 (and_134_out, X0, not_5_out, X3, Y0, Y1, Y2);
  xor xor_39 (xor_39_out, and_135_out, xor_40_out);
  and and_135 (and_135_out, Y1, X1);
  and and_136 (and_136_out, xor_40_out, and_135_out);
  and and_137 (and_137_out, xor_39_out, and_140_out);
  and and_138 (and_138_out, not_4_out, X1, not_6_out, not_7_out, Y0, Y1);
  and and_139 (and_139_out, Y0, X2);
  xor xor_40 (xor_40_out, and_139_out, and_143_out);
  and and_140 (and_140_out, Y2, X0);
  and and_141 (and_141_out, and_143_out, and_139_out);
  or or_33 (or_33_out, and_141_out, and_136_out);
  xor xor_41 (xor_18_out[2], xor_39_out, and_140_out);
  and and_142 (and_142_out, X0, X1, X2, not_7_out, not_1_out, not_2_out);
  and and_143 (and_143_out, and_146_out, and_145_out);
  and and_144 (and_144_out, X0, not_5_out, X2, X3, Y0, Y2);
  and and_145 (and_145_out, Y1, X0);
  and and_146 (and_146_out, Y0, X1);
  xor xor_42 (xor_18_out[1], and_146_out, and_145_out);
  and and_147 (and_147_out, X0, X1, not_7_out, not_2_out, Y2);
  and and_148 (and_148_out, not_5_out, not_6_out, X3, not_1_out, Y1, Y2);
  and and_149 (xor_18_out[0], Y0, X0);
  and and_150 (and_150_out, X1, X2, X3, not_1_out, Y2);
  and and_151 (and_151_out, X1, not_1_out, not_2_out, Y2);
  and and_152 (and_152_out, X1, not_6_out, not_7_out, Y2);
  and and_153 (and_153_out, not_4_out, not_5_out, X2, not_7_out, Y0, Y1, not_3_out);
  and and_154 (and_154_out, not_4_out, X1, X2, not_7_out, Y0, not_2_out, Y2);
  and and_155 (and_155_out, not_4_out, not_5_out, X3, Y0, Y1, Y2);
  and and_156 (and_156_out, not_4_out, X1, not_6_out, X3, Y0, Y1);
  and and_157 (and_157_out, not_4_out, not_5_out, not_6_out, X3, Y0, Y2);
  and and_158 (and_158_out, X0, X1, X2, not_7_out, Y1, not_3_out);
  and and_159 (and_159_out, X0, X1, not_6_out, X3, not_2_out, Y2);
  or or_34 (R3, and_153_out, and_154_out, and_155_out, and_156_out, and_157_out, and_158_out, and_159_out, and_160_out, and_161_out, and_162_out, and_163_out, and_164_out, and_165_out, and_166_out, and_167_out, and_168_out, and_169_out);
  and and_160 (and_160_out, X0, not_5_out, X2, X3, Y1, not_3_out);
  and and_161 (and_161_out, X0, not_5_out, X2, X3, not_2_out, Y2);
  Multiplexer #(.Selector_Bits(4), .Bits(8)) multiplexer_1 (
    .sel(S), .in_0(xor_18_out), .in_1({in_24, R5, R4, R3, Q3, Q2, Q1, Q0}),
    .in_2({in_4, in_3, in_2, xor_11_out}), .in_3({xor_9_out[7], in_6, in_5, in_8, xor_9_out[3:0]}),
    .in_4({in_39[2:0], X3, and_51_out}), .in_5({in_40, and_57_out}), .in_6({_0_2, or_16_out[0]}),
    .in_7({_0_3, or_17_out[0]}), .in_8({_4, and_72_out[0]}), .in_9({in_35, not_20_out}),
    .in_10({in_34, xor_3_out}), .in_11({in_33, or_4_out}), .in_12({in_32, and_9_out}),
    .in_13({in_37[2:0], xor_1_out}), .in_14({in_38, or_3_out}), .in_15(in_36), .out(Output));
  and and_162 (and_162_out, X0, X1, X2, X3, Y1, Y2);
  and and_163 (and_163_out, X0, not_5_out, not_6_out, not_7_out, not_1_out);
  and and_164 (and_164_out, X0, not_5_out, not_7_out, Y1, Y2);
  and and_165 (and_165_out, X0, not_5_out, not_6_out, not_7_out, Y1);
  and and_166 (and_166_out, X0, not_5_out, not_6_out, not_7_out, Y2);
  and and_167 (and_167_out, X0, not_1_out, Y1, not_3_out);
  and and_168 (and_168_out, X0, X2, not_1_out, Y2);
  and and_169 (and_169_out, X0, X3, not_1_out, Y2);
  or or_35 (or_35_out, Output[6], Output[7]);
  or or_36 (or_36_out, or_37_out, or_35_out);
  or or_37 (or_37_out, Output[4], Output[5]);
  not not_33 (out_26, or_39_out);
  or or_38 (or_38_out, Output[2], Output[3]);
  or or_39 (or_39_out, or_40_out, or_36_out);
  or or_40 (or_40_out, or_41_out, or_38_out);
  or or_41 (or_41_out, Output[0], Output[1]);

  // Notes on the sheet:
  //   _1: default 1
  //   _3: default 1
endmodule
